// Logisim project alu.circ as structural Verilog
module aluReloaded (
  input  [7:0] A,
  input  [7:0] B,
  input  [7:0] C,
  input  [7:0] D,
  output [7:0] F,
  output [7:0] E
);

  wire [7:0] multiplexer_1_out, multiplexer_2_out;

  Multiplexer #(.select(1), .width(8)) multiplexer_1 (.in0(E), .in1(A), .out(multiplexer_1_out));  // open: sel
  Multiplexer #(.select(1), .width(8)) multiplexer_2 (.in0(B), .in1(F), .out(multiplexer_2_out));  // open: sel
  Adder #(.width(8)) adder_1 (.a(multiplexer_1_out), .b(multiplexer_2_out), .out(E));  // open: cin, cout
  Adder #(.width(8)) adder_2 (.a(C), .b(D), .out(F));  // open: cin, cout
endmodule

module registers (
  input  [7:0] E,
  input  [7:0] F,
  input  [5:0] InSel_EF,
  input  [11:0] OutSel_ABCD,
  output [7:0] D,
  output [7:0] C,
  output [7:0] B,
  output [7:0] A
);

  wire undriven, undriven_2, undriven_3, undriven_4, undriven_5, undriven_6, undriven_7, undriven_8;
  wire [7:0] demultiplexer_1_out0, demultiplexer_1_out1, demultiplexer_1_out2, demultiplexer_1_out3,
       demultiplexer_1_out4, demultiplexer_1_out5, demultiplexer_1_out6, demultiplexer_1_out7, register_1_q,
       register_2_q, register_3_q, register_4_q, register_5_q, register_7_q, register_8_q;

  Demultiplexer #(.select(3), .width(8), .tristate("false")) demultiplexer_1 (
    .out0(demultiplexer_1_out0), .out1(demultiplexer_1_out1), .out2(demultiplexer_1_out2),
    .out3(demultiplexer_1_out3), .out4(demultiplexer_1_out4), .out5(demultiplexer_1_out5),
    .out6(demultiplexer_1_out6), .out7(demultiplexer_1_out7), .in(F), .sel(InSel_EF[5:3]));
  Demultiplexer #(.select(3), .width(8), .tristate("false")) demultiplexer_2 (
    .out0(demultiplexer_1_out0), .out1(demultiplexer_1_out1), .out2(demultiplexer_1_out2),
    .out3(demultiplexer_1_out3), .out4(demultiplexer_1_out4), .out5(demultiplexer_1_out5),
    .out6(demultiplexer_1_out6), .out7(demultiplexer_1_out7), .in(E), .sel(InSel_EF[2:0]));
  Register #(.width(8), .trigger("rising")) register_1 (
    .D(demultiplexer_1_out0), .Q(register_1_q), .clk(undriven_2));  // open: en, clr
  Register #(.width(8), .trigger("rising")) register_2 (
    .D(demultiplexer_1_out1), .Q(register_2_q), .clk(undriven_3));  // open: en, clr
  Register #(.width(8), .trigger("rising")) register_3 (
    .D(demultiplexer_1_out2), .Q(register_3_q), .clk(undriven_4));  // open: en, clr
  Register #(.width(8), .trigger("rising")) register_4 (
    .D(demultiplexer_1_out3), .Q(register_4_q), .clk(undriven_5));  // open: en, clr
  Register #(.width(8), .trigger("rising")) register_5 (
    .D(demultiplexer_1_out4), .Q(register_5_q), .clk(undriven_6));  // open: en, clr
  Register #(.width(8), .trigger("rising")) register_6 (
    .D(demultiplexer_1_out5), .Q(register_5_q), .clk(undriven));  // open: en, clr
  Register #(.width(8), .trigger("rising")) register_7 (
    .D(demultiplexer_1_out6), .Q(register_7_q), .clk(undriven_7));  // open: en, clr
  Register #(.width(8), .trigger("rising")) register_8 (
    .D(demultiplexer_1_out7), .Q(register_8_q), .clk(undriven_8));  // open: en, clr
  Multiplexer #(.select(3), .width(8)) multiplexer_1 (
    .in0(register_1_q), .in1(register_2_q), .in2(register_3_q), .in3(register_4_q), .in4(register_5_q),
    .in5(register_5_q), .in6(register_7_q), .in7(register_8_q), .out(D), .sel(OutSel_ABCD[11:9]));
  Multiplexer #(.select(3), .width(8)) multiplexer_2 (
    .in0(register_1_q), .in1(register_2_q), .in2(register_3_q), .in3(register_4_q), .in4(register_5_q),
    .in5(register_5_q), .in6(register_7_q), .in7(register_8_q), .out(C), .sel(OutSel_ABCD[8:6]));
  Multiplexer #(.select(3), .width(8)) multiplexer_3 (
    .in0(register_1_q), .in1(register_2_q), .in2(register_3_q), .in3(register_4_q), .in4(register_5_q),
    .in5(register_5_q), .in6(register_7_q), .in7(register_8_q), .out(B), .sel(OutSel_ABCD[5:3]));
  Multiplexer #(.select(3), .width(8)) multiplexer_4 (
    .in0(register_1_q), .in1(register_2_q), .in2(register_3_q), .in3(register_4_q), .in4(register_5_q),
    .in5(register_5_q), .in6(register_7_q), .in7(register_8_q), .out(A), .sel(OutSel_ABCD[2:0]));
endmodule
