// Logisim project fifth.circ as structural Verilog: 14 circuits, main circuit main
module main (
);

  wire clock_1_out, processor_1_mrw, processor_1_msync;
  wire [6:0] processor_1_addressout;
  wire [15:0] ram_1_data;

  processor processor_1 (
    .Clock(clock_1_out), .DataIn(ram_1_data), .AddressOut(processor_1_addressout), .MRW(processor_1_mrw),
    .MSync(processor_1_msync));
  Clock #(.highDuration(1), .lowDuration(1)) clock_1 (.out(clock_1_out));
  // Probe on processor_1_addressout
  RAM #(.addrWidth(7), .dataWidth(16), .bus("combined")) ram_1 (
    .addr(processor_1_addressout), .data(ram_1_data), .clk(processor_1_mrw), .ld(processor_1_msync));  // open: sel, clr

  // Notes on the sheet:
  //   Data
  //   Address
endmodule

module aluReloaded (
  input  [15:0] A,
  input  [15:0] B,
  input  [15:0] C,
  input  [15:0] D,
  input  [1:0] ALUtoEF,
  input  ALUsum,
  output [15:0] F,
  output [15:0] E
);

  wire [15:0] adder_1_out, adder_2_out, multiplexer_1_out, multiplexer_2_out;

  Multiplexer #(.select(1), .width(16)) multiplexer_1 (
    .in0(A), .in1(adder_1_out), .out(multiplexer_1_out), .sel(ALUsum));
  Multiplexer #(.select(1), .width(16)) multiplexer_2 (
    .in0(B), .in1(adder_2_out), .out(multiplexer_2_out), .sel(ALUsum));
  Adder #(.width(16)) adder_1 (.a(multiplexer_1_out), .b(multiplexer_2_out), .out(adder_1_out));  // open: cin, cout
  Adder #(.width(16)) adder_2 (.a(C), .b(D), .out(adder_2_out));  // open: cin, cout
  assign F = ALUtoEF[0] ? adder_2_out : 16'bz;  // Controlled_Buffer controlled_buffer_1
  assign E = ALUtoEF[1] ? adder_1_out : 16'bz;  // Controlled_Buffer controlled_buffer_2
endmodule

module processor (
  input  [15:0] DataIn,
  input  Clock,
  output [6:0] AddressOut,
  output MRW,
  output MSync
);

  wire undriven_2, undriven_3, undriven_4, undriven_5;
  wire [15:0] demultiplexer_1_out0, demultiplexer_2_out1, registers_1_outbus, registers_1_outbus2, undriven;

  Demultiplexer #(.select(1), .width(16), .tristate("false")) demultiplexer_1 (
    .out0(demultiplexer_1_out0), .in(undriven), .sel(undriven_2));  // open: out1
  registers registers_1 (
    .InBuff(undriven), .reset(undriven_3), .outBus2(registers_1_outbus2), .outBus(registers_1_outbus));  // open: regIn, regInSel, regOutSel, regOut, regOutSel2, regOut2
  PC pc_1 (.PCinc(undriven_4), .reset(undriven_5));  // open: dir
  Demultiplexer #(.select(1), .width(16), .tristate("false")) demultiplexer_2 (
    .out0(demultiplexer_1_out0), .out1(demultiplexer_2_out1), .in(DataIn), .sel(1'b0));

  // Notes on the sheet:
  //   Data
  //   Data 2
  //   Address
endmodule

module registers (
  input  reset,
  input  [15:0] InBuff,
  input  [2:0] regOutSel,
  input  regOut,
  input  [2:0] regOutSel2,
  input  regOut2,
  input  regIn,
  input  [2:0] regInSel,
  output [15:0] outBus2,
  output [15:0] outBus
);

  wire regselector_1__0, regselector_1__1, regselector_1__2, regselector_1__3, regselector_1__4,
       regselector_1__5, regselector_1__6, regselector_1__7;
  wire [15:0] register_1_q, register_2_q, register_3_q, register_4_q, register_5_q, register_6_q,
       register_7_q, register_8_q;

  Register #(.width(16), .trigger("rising")) register_1 (
    .D(InBuff), .Q(register_1_q), .clk(regselector_1__0), .clr(reset));  // open: en
  Register #(.width(16), .trigger("rising")) register_2 (
    .D(InBuff), .Q(register_2_q), .clk(regselector_1__1), .clr(reset));  // open: en
  Register #(.width(16), .trigger("rising")) register_3 (
    .D(InBuff), .Q(register_3_q), .clk(regselector_1__2), .clr(reset));  // open: en
  Register #(.width(16), .trigger("rising")) register_4 (
    .D(InBuff), .Q(register_4_q), .clk(regselector_1__3), .clr(reset));  // open: en
  Register #(.width(16), .trigger("rising")) register_5 (
    .D(InBuff), .Q(register_5_q), .clk(regselector_1__4), .clr(reset));  // open: en
  Register #(.width(16), .trigger("rising")) register_6 (
    .D(InBuff), .Q(register_6_q), .clk(regselector_1__5), .clr(reset));  // open: en
  Register #(.width(16), .trigger("rising")) register_7 (
    .D(InBuff), .Q(register_7_q), .clk(regselector_1__6), .clr(reset));  // open: en
  Register #(.width(16), .trigger("rising")) register_8 (
    .D(InBuff), .Q(register_8_q), .clk(regselector_1__7), .clr(reset));  // open: en
  RegSelector regselector_1 (
    .RegIn(regIn), .Reg(regInSel), ._7(regselector_1__7), ._6(regselector_1__6), ._5(regselector_1__5),
    ._4(regselector_1__4), ._3(regselector_1__3), ._2(regselector_1__2), ._1(regselector_1__1),
    ._0(regselector_1__0));
  OutBusSel outbussel_1 (
    ._0(register_1_q), ._1(register_2_q), ._2(register_3_q), ._3(register_4_q), ._4(register_5_q),
    ._5(register_6_q), ._6(register_7_q), ._7(register_8_q), .OutBus(regOutSel), .OutBus2(regOutSel2),
    .regOut(regOut), .regOut2(regOut2), .outBus2_2(outBus2), .outBus_2(outBus));
endmodule

module RegSelector (
  input  RegIn,
  input  [2:0] Reg,
  output _7,
  output _6,
  output _5,
  output _4,
  output _3,
  output _2,
  output _1,
  output _0
);

  wire decoder_1_out0, decoder_1_out1, decoder_1_out2, decoder_1_out3, decoder_1_out4, decoder_1_out5,
       decoder_1_out6, decoder_1_out7;

  Decoder #(.select(3), .tristate("false")) decoder_1 (
    .out0(decoder_1_out0), .out1(decoder_1_out1), .out2(decoder_1_out2), .out3(decoder_1_out3),
    .out4(decoder_1_out4), .out5(decoder_1_out5), .out6(decoder_1_out6), .out7(decoder_1_out7), .sel(Reg));
  and and_1 (_0, decoder_1_out0, RegIn);
  and and_2 (_1, decoder_1_out1, RegIn);
  and and_3 (_2, decoder_1_out2, RegIn);
  and and_4 (_3, decoder_1_out3, RegIn);
  and and_5 (_4, decoder_1_out4, RegIn);
  and and_6 (_5, decoder_1_out5, RegIn);
  and and_7 (_6, decoder_1_out6, RegIn);
  and and_8 (_7, decoder_1_out7, RegIn);
endmodule

module BusSelector (
  input  [15:0] E,
  input  [15:0] F,
  input  [2:0] fromE,
  input  [2:0] fromF,
  output [15:0] _0,
  output [15:0] _1,
  output [15:0] _2,
  output [15:0] _3,
  output [15:0] _4,
  output [15:0] _5,
  output [15:0] _6,
  output [15:0] _7
);

  Demultiplexer #(.select(3), .width(16), .tristate("true")) demultiplexer_1 (
    .out0(_0), .out1(_1), .out2(_2), .out3(_3), .out4(_4), .out5(_5), .out6(_6), .out7(_7), .in(E),
    .sel(fromE));
  Demultiplexer #(.select(3), .width(16), .tristate("true")) demultiplexer_2 (
    .out0(_0), .out1(_1), .out2(_2), .out3(_3), .out4(_4), .out5(_5), .out6(_6), .out7(_7), .in(F),
    .sel(fromF));
endmodule

module OutBusSel (
  input  [15:0] _0,
  input  [15:0] _1,
  input  [15:0] _2,
  input  [15:0] _3,
  input  [15:0] _4,
  input  [15:0] _5,
  input  [15:0] _6,
  input  [15:0] _7,
  input  [2:0] OutBus,
  input  [2:0] OutBus2,
  input  regOut,
  input  regOut2,
  output [15:0] outBus2_2,
  output [15:0] outBus_2
);

  wire [15:0] multiplexer_1_out, multiplexer_2_out;

  Multiplexer #(.select(3), .width(16)) multiplexer_1 (
    .in0(_0), .in1(_1), .in2(_2), .in3(_3), .in4(_4), .in5(_5), .in6(_6), .in7(_7), .out(multiplexer_1_out),
    .sel(OutBus));
  Multiplexer #(.select(3), .width(16)) multiplexer_2 (
    .in0(_0), .in1(_1), .in2(_2), .in3(_3), .in4(_4), .in5(_5), .in6(_6), .in7(_7), .out(multiplexer_2_out),
    .sel(OutBus2));
  assign outBus_2 = regOut ? multiplexer_1_out : 16'bz;  // Controlled_Buffer controlled_buffer_1
  assign outBus2_2 = regOut2 ? multiplexer_2_out : 16'bz;  // Controlled_Buffer controlled_buffer_2
endmodule

module ProcessorRegisters (
  input  \reg ,
  input  Jump,
  input  [6:0] Address,
  input  MemAdd,
  input  [15:0] MBRIn,
  input  [15:0] IRIn,
  input  [3:0] RegIn_PC_MAR_MBR_IR,
  input  [1:0] RegOut_MAR_MBR,
  output [6:0] MARout,
  output [15:0] MBRout,
  output [15:0] IRout
);

  wire [6:0] adder_1_out, MAR_q, multiplexer_1_out, multiplexer_2_out, PC_q;
  wire [15:0] MBR_q;

  Adder #(.width(7)) adder_1 (.a(PC_q), .b(7'b0000001), .out(adder_1_out));  // open: cin, cout
  Multiplexer #(.select(1), .width(7)) multiplexer_1 (
    .in0(adder_1_out), .in1(Address), .out(multiplexer_1_out), .sel(Jump));
  Register #(.width(7), .trigger("rising")) PC (
    .D(multiplexer_1_out), .Q(PC_q), .clk(RegIn_PC_MAR_MBR_IR[3]), .clr(\reg ));  // open: en
  Multiplexer #(.select(1), .width(7)) multiplexer_2 (.in0(PC_q), .in1(Address), .out(multiplexer_2_out), .sel(MemAdd));
  Register #(.width(7), .trigger("rising")) MAR (
    .D(multiplexer_2_out), .Q(MAR_q), .clk(RegIn_PC_MAR_MBR_IR[2]), .clr(\reg ));  // open: en
  Register #(.width(16), .trigger("rising")) MBR (
    .D(MBRIn), .Q(MBR_q), .clk(RegIn_PC_MAR_MBR_IR[1]), .clr(\reg ));  // open: en
  Register #(.width(16), .trigger("rising")) IR (
    .D(IRIn), .Q(IRout), .clk(RegIn_PC_MAR_MBR_IR[0]), .clr(\reg ));  // open: en
  assign MARout = RegOut_MAR_MBR[1] ? MAR_q : 7'bz;  // Controlled_Buffer controlled_buffer_1
  assign MBRout = RegOut_MAR_MBR[0] ? MBR_q : 16'bz;  // Controlled_Buffer controlled_buffer_2
endmodule

module ControlU (
  input  in_1,
  input  in_2,
  output MemRW,
  output sync
);

  wire [1:0] undriven_2;
  wire [4:0] adder_1_out, multiplexer_1_out, register_1_q, undriven;
  wire [15:0] rom_1_data;

  Adder #(.width(5)) adder_1 (.a(register_1_q), .b(5'b00001), .out(adder_1_out));  // open: cin, cout
  Multiplexer #(.select(2), .width(5)) multiplexer_1 (
    .in0(adder_1_out), .in1(undriven), .in2({5{1'b0}}), .out(multiplexer_1_out), .sel(undriven_2));  // open: in3
  Register #(.width(5), .trigger("rising")) register_1 (
    .D(multiplexer_1_out), .Q(register_1_q), .clk(in_1), .clr(in_2));  // open: en
  ROM #(.addrWidth(5), .dataWidth(16)) rom_1 (.addr(register_1_q), .data(rom_1_data));  // open: sel

  // Notes on the sheet:
  //   contents of rom_1 (hex, n*v repeats v):
  //   4b00 9801 14*0 4 4b00 2700 482 4*0 4 4800 2c00 d02
endmodule

module instDecoder (
  input  [15:0] IRin,
  output [6:0] addressMEM,
  output movM,
  output [2:0] opCode,
  output dir,
  output [2:0] reg1,
  output [2:0] reg2
);

  wire decoder_1_out1, decoder_1_out2, decoder_1_out3;
  wire [1:0] controlled_buffer_1_out;
  wire [2:0] controlled_buffer_4_out;
  wire [6:0] controlled_buffer_2_out, controlled_buffer_3_out;

  Decoder #(.select(3), .tristate("false")) decoder_1 (
    .out0(movM), .out1(decoder_1_out1), .out2(decoder_1_out2), .out3(decoder_1_out3), .sel(IRin[15:13]));  // open: out4, out5, out6, out7
  assign {reg1, dir, addressMEM, controlled_buffer_1_out} = movM ? IRin[12:0] : 13'bz;  // Controlled_Buffer controlled_buffer_1
  assign {reg1, reg2, controlled_buffer_2_out} = decoder_1_out1 ? IRin[12:0] : 13'bz;  // Controlled_Buffer controlled_buffer_2
  assign {reg1, reg2, controlled_buffer_3_out} = decoder_1_out2 ? IRin[12:0] : 13'bz;  // Controlled_Buffer controlled_buffer_3
  assign {reg1, addressMEM, controlled_buffer_4_out} = decoder_1_out3 ? IRin[12:0] : 13'bz;  // Controlled_Buffer controlled_buffer_4

  assign opCode = IRin[15:13];
endmodule

module memHiJacker (
  input  dir,
  input  movM,
  input  MRW,
  output MRW_2
);

  wire not_1_out, or_1_out;

  or or_1 (or_1_out, movM, 1'b0);
  assign MRW_2 = or_1_out ? dir : 1'bz;  // Controlled_Buffer controlled_buffer_1
  not not_1 (not_1_out, or_1_out);
  assign MRW_2 = not_1_out ? MRW : 1'bz;  // Controlled_Buffer controlled_buffer_2
endmodule

module busSelector (
  input  [2:0] \reg ,
  input  dir,
  input  MovM,
  output [2:0] reg1,
  output [11:0] ABCD
);

  wire controlled_buffer_1_out, not_1_out;

  assign controlled_buffer_1_out = not_1_out ? 1'b0 : 1'bz;  // Controlled_Buffer controlled_buffer_1
  not not_1 (not_1_out, MovM);
  assign controlled_buffer_1_out = MovM ? dir : 1'bz;  // Controlled_Buffer controlled_buffer_2
  Demultiplexer #(.select(1), .width(3), .tristate("false")) demultiplexer_1 (
    .out0(reg1), .out1(ABCD[11:9]), .in(\reg ), .sel(controlled_buffer_1_out));

  // Notes on the sheet:
  //   1 registro a memoria
endmodule

module memHiJacker2 (
  input  dir,
  input  MRW,
  input  Msync,
  output regOut,
  output MRW_2,
  output Msync_2
);

  wire not_1_out;

  not not_1 (not_1_out, Msync);
  and and_1 (regOut, dir, not_1_out);

  assign MRW_2 = MRW;
  assign Msync_2 = Msync;
endmodule

module PC (
  input  PCinc,
  input  reset,
  output [6:0] dir
);

  wire [6:0] adder_1_out;

  Register #(.width(7), .trigger("rising")) PC (.D(adder_1_out), .Q(dir), .clk(PCinc), .clr(reset));  // open: en
  Adder #(.width(7)) adder_1 (.a(dir), .b(7'b0000001), .out(adder_1_out));  // open: cin, cout
endmodule
